// Logisim project DZ.circ as structural Verilog: 1 circuit, main circuit main
module main (
  input  [1:0] in_1,
  input  [1:0] in_2
);

  wire comparator_1_eq;

  Comparator #(.width(2)) comparator_1 (.a(in_1), .b(in_2), .eq(comparator_1_eq));  // open: gt, lt
  Register #(.width(2)) register_1 (.D(in_2), .clk(comparator_1_eq));  // open: en, Q, clr
endmodule
