// Logisim project ДЗ3.circ as structural Verilog: 1 circuit, main circuit main
module main (
);

  wire clock_1_out, comparator_1_eq, comparator_2_eq, comparator_3_eq, comparator_4_eq, comparator_5_eq,
       comparator_6_eq, comparator_7_eq, comparator_8_eq, comparator_9_eq, comparator_10_eq,
       comparator_11_eq, comparator_12_eq, comparator_13_eq;
  wire [2:0] counter_1_q, subtractor_1_out;
  wire [7:0] multiplexer_1_out, random_1_out, register_1_q, register_2_q, register_3_q, register_4_q,
       register_5_q, register_6_q, register_7_q, register_8_q, register_9_q, register_10_q, register_11_q,
       register_12_q, register_13_q;

  Clock clock_1 (.out(clock_1_out));
  Counter #(.width(3), .max('h5)) counter_1 (.Q(counter_1_q), .clk(clock_1_out));  // open: load, D, count, carry, clr
  // Probe on random_1_out
  Random random_1 (.clk(clock_1_out), .out(random_1_out));  // open: next, clr
  Subtractor #(.width(3)) subtractor_1 (.a(counter_1_q), .b(3'b001), .out(subtractor_1_out));  // open: bin, bout
  Comparator #(.width(3)) comparator_1 (.a(subtractor_1_out), .b(3'b000), .eq(comparator_1_eq));  // open: gt, lt
  Comparator #(.width(3)) comparator_2 (.a(subtractor_1_out), .b(3'b001), .eq(comparator_2_eq));  // open: gt, lt
  Comparator #(.width(3)) comparator_3 (.a(subtractor_1_out), .b(3'b001), .eq(comparator_3_eq));  // open: gt, lt
  Comparator #(.width(3)) comparator_4 (.a(subtractor_1_out), .b(3'b010), .eq(comparator_4_eq));  // open: gt, lt
  Comparator #(.width(3)) comparator_5 (.a(subtractor_1_out), .b(3'b011), .eq(comparator_5_eq));  // open: gt, lt
  Comparator #(.width(3)) comparator_6 (.a(subtractor_1_out), .b(3'b100), .eq(comparator_6_eq));  // open: gt, lt
  Comparator #(.width(3)) comparator_7 (.a(subtractor_1_out), .b(3'b111), .eq(comparator_7_eq));  // open: gt, lt
  Register register_1 (.D(random_1_out), .Q(register_1_q), .clk(comparator_1_eq));  // open: en, clr
  Register register_2 (.D(register_1_q), .Q(register_2_q), .clk(comparator_2_eq));  // open: en, clr
  Register register_3 (.D(random_1_out), .Q(register_3_q), .clk(comparator_3_eq));  // open: en, clr
  Register register_4 (.D(random_1_out), .Q(register_4_q), .clk(comparator_4_eq));  // open: en, clr
  Register register_5 (.D(random_1_out), .Q(register_5_q), .clk(comparator_5_eq));  // open: en, clr
  Register register_6 (.D(random_1_out), .Q(register_6_q), .clk(comparator_6_eq));  // open: en, clr
  Register register_7 (.D(random_1_out), .Q(register_7_q), .clk(comparator_7_eq));  // open: en, clr
  Comparator #(.width(3)) comparator_8 (.a(subtractor_1_out), .b(3'b000), .eq(comparator_8_eq));  // open: gt, lt
  Comparator #(.width(3)) comparator_9 (.a(subtractor_1_out), .b(3'b000), .eq(comparator_9_eq));  // open: gt, lt
  Comparator #(.width(3)) comparator_10 (.a(subtractor_1_out), .b(3'b000), .eq(comparator_10_eq));  // open: gt, lt
  Comparator #(.width(3)) comparator_11 (.a(subtractor_1_out), .b(3'b000), .eq(comparator_11_eq));  // open: gt, lt
  Comparator #(.width(3)) comparator_12 (.a(subtractor_1_out), .b(3'b000), .eq(comparator_12_eq));  // open: gt, lt
  Comparator #(.width(3)) comparator_13 (.a(subtractor_1_out), .b(3'b000), .eq(comparator_13_eq));  // open: gt, lt
  Register register_8 (.D(register_7_q), .Q(register_8_q), .clk(comparator_8_eq));  // open: en, clr
  Register register_9 (.D(register_6_q), .Q(register_9_q), .clk(comparator_9_eq));  // open: en, clr
  Register register_10 (.D(register_5_q), .Q(register_10_q), .clk(comparator_10_eq));  // open: en, clr
  Register register_11 (.D(register_4_q), .Q(register_11_q), .clk(comparator_11_eq));  // open: en, clr
  Register register_12 (.D(register_3_q), .Q(register_12_q), .clk(comparator_12_eq));  // open: en, clr
  Register register_13 (.D(register_2_q), .Q(register_13_q), .clk(comparator_13_eq));  // open: en, clr
  // Probe on multiplexer_1_out
  Multiplexer #(.select(3), .width(8)) multiplexer_1 (
    .in0(register_8_q), .in1(register_9_q), .in2(register_10_q), .in3(register_11_q), .in4(register_12_q),
    .in7(register_13_q), .out(multiplexer_1_out), .sel(subtractor_1_out), .en(1'b1));  // open: in5, in6
endmodule
