// Logisim project дз.circ as structural Verilog: 1 circuit, main circuit main
module main (
  input  [2:0] in_1,
  input  [2:0] in_2,
  output [7:0] out_3
);

  wire clock_1_out, comparator_1_eq, transistor_1_out;
  wire [7:0] random_1_out;

  Pull_Resistor pull_resistor_1 (.node(in_1[2]));
  Pull_Resistor pull_resistor_2 (.node(in_2[0]));
  Pull_Resistor pull_resistor_3 (.node(in_2[2]));
  Pull_Resistor pull_resistor_4 (.node(in_1[0]));
  Comparator #(.width(1)) comparator_1 (.a(in_1[1]), .b(in_2[1]), .eq(comparator_1_eq));  // open: gt, lt
  Random random_1 (.clk(clock_1_out), .out(random_1_out));  // open: next, clr
  Clock clock_1 (.out(clock_1_out));
  Register register_1 (.D(random_1_out), .Q(out_3), .clk(transistor_1_out));  // open: en, clr
  Transistor #(.\type ("n")) transistor_1 (.in(clock_1_out), .out(transistor_1_out), .gate(comparator_1_eq));
  // Probe on out_3
endmodule
