// Logisim project лол.circ as structural Verilog: 1 circuit, main circuit main
module main (
  output [7:0] out_1
);

  wire clock_1_out, comparator_1_eq, comparator_2_eq, comparator_3_eq, comparator_4_eq, comparator_5_eq,
       comparator_6_eq, comparator_7_eq, comparator_8_eq, comparator_9_eq;
  wire [1:0] counter_1_q, subtractor_1_out;
  wire [7:0] random_1_out, register_1_q, register_2_q, register_3_q, register_4_q, register_5_q,
       register_6_q, register_7_q, register_8_q, register_9_q;

  Clock clock_1 (.out(clock_1_out));
  // Probe on counter_1_q
  Counter #(.width(2), .max('h3)) counter_1 (.Q(counter_1_q), .clk(clock_1_out));  // open: load, D, count, carry, clr
  Random random_1 (.clk(clock_1_out), .out(random_1_out));  // open: next, clr
  Subtractor #(.width(2)) subtractor_1 (.a(counter_1_q), .b(2'b01), .out(subtractor_1_out));  // open: bin, bout
  // Probe on random_1_out
  Comparator #(.width(2)) comparator_1 (.a(subtractor_1_out), .b(2'b00), .eq(comparator_1_eq));  // open: gt, lt
  Comparator #(.width(2)) comparator_2 (.a(subtractor_1_out), .b(2'b01), .eq(comparator_2_eq));  // open: gt, lt
  Register register_1 (.D(random_1_out), .Q(register_1_q), .clk(comparator_3_eq));  // open: en, clr
  Comparator #(.width(2)) comparator_3 (.a(subtractor_1_out), .b(2'b01), .eq(comparator_3_eq));  // open: gt, lt
  Register register_2 (.D(random_1_out), .Q(register_2_q), .clk(comparator_4_eq));  // open: en, clr
  Comparator #(.width(2)) comparator_4 (.a(subtractor_1_out), .b(2'b10), .eq(comparator_4_eq));  // open: gt, lt
  Register register_3 (.D(random_1_out), .Q(register_3_q), .clk(comparator_5_eq));  // open: en, clr
  Comparator #(.width(2)) comparator_5 (.a(subtractor_1_out), .b(2'b11), .eq(comparator_5_eq));  // open: gt, lt
  Register register_4 (.D(random_1_out), .Q(register_4_q), .clk(comparator_1_eq));  // open: en, clr
  Register register_5 (.D(register_4_q), .Q(register_5_q), .clk(comparator_2_eq));  // open: en, clr
  Register register_6 (.D(register_1_q), .Q(register_6_q), .clk(comparator_6_eq));  // open: en, clr
  Comparator #(.width(2)) comparator_6 (.a(subtractor_1_out), .b(2'b00), .eq(comparator_6_eq));  // open: gt, lt
  Register register_7 (.D(register_3_q), .Q(register_7_q), .clk(comparator_7_eq));  // open: en, clr
  Comparator #(.width(2)) comparator_7 (.a(subtractor_1_out), .b(2'b00), .eq(comparator_7_eq));  // open: gt, lt
  Register register_8 (.D(register_5_q), .Q(register_8_q), .clk(comparator_8_eq));  // open: en, clr
  Comparator #(.width(2)) comparator_8 (.a(subtractor_1_out), .b(2'b00), .eq(comparator_8_eq));  // open: gt, lt
  Register register_9 (.D(register_2_q), .Q(register_9_q), .clk(comparator_9_eq));  // open: en, clr
  Comparator #(.width(2)) comparator_9 (.a(subtractor_1_out), .b(2'b00), .eq(comparator_9_eq));  // open: gt, lt
  // Probe on out_1
  Multiplexer #(.select(2), .width(8)) multiplexer_1 (
    .in0(register_6_q), .in1(register_7_q), .in2(register_8_q), .in3(register_9_q), .out(out_1),
    .sel(subtractor_1_out), .en(1'b1));
endmodule
